// Logisim project cpu.circ as structural Verilog: 1 circuit, main circuit cpu
module cpu (
  input  Rest
);

  wire alu_1_zero, alucontroller_1_sh_amount, and_1_out, and_2_out, and_3_out, and_4_out, and_5_out, AO,
       cache_1_p5, cache_1_p8, clk, comparator_1_eq, comparator_2_eq, comparator_3_eq, controller_1_alusrc,
       controller_1_branch, controller_1_jump, controller_1_lb, controller_1_memtoreg, controller_1_regdst,
       controller_1_regwren, id_ex_1_alusrcout, id_ex_1_branchout, id_ex_1_jumpout, id_ex_1_regdstout,
       id_ex_1_sh_amountout, LB, memToReg, multiplexer_1_out, not_1_out, or_1_out, regfile_1_p5,
       regfile_1_p7, RType;
  wire [1:0] alu_1_result;
  wire [3:0] bit_extender_5_out, controller_1_memwrmask, id_ex_1_memwrmaskout, multiplexer_8_out,
       oneclockdelay_1_dataout_2, shifter_4_out;
  wire [4:0] alucontroller_1_alu_out, bit_extender_4_out, id_ex_1_alu_outout, multiplexer_3_out,
       multiplexer_4_out, oneclockdelay_2_dataout_2, oneclockdelay_2_dataout_3, shifter_5_out;
  wire [5:0] oneclockdelay_2_dataout;
  wire [7:0] multiplexer_13_out;
  wire [25:16] oneclockdelay_2_dataout_4;
  wire [27:0] oneclockdelay_1_dataout;
  wire [31:0] adder_1_out, adder_2_out, bit_extender_1_out, bit_extender_2_out, bit_extender_3_out,
       bit_extender_6_out, cache_1_p6, cache_1_p7, cache_1_p9, id_ex_1_extendedbitsout, id_ex_1_extendedout,
       id_ex_1_readdata1out, id_ex_1_readdata2out, MemData, multiplexer_2_out, multiplexer_5_out,
       multiplexer_6_out, multiplexer_7_out, multiplexer_9_out, multiplexer_10_out, multiplexer_11_out,
       multiplexer_12_out, multiplexer_14_out, multiplexer_15_out, pc, regfile_1_p9, regfile_1_p10,
       shifter_1_out, shifter_2_out, shifter_3_out, shifter_6_out, signextend_1_extended, undriven, xor_1_out;
  wire [31:2] alu_1_result_2;
  wire [31:26] oneclockdelay_2_dataout_5;

  Multiplexer multiplexer_1 (.in0(1'b1), .in1(1'b0), .out(multiplexer_1_out), .sel(and_3_out));
  Multiplexer #(.width(32)) multiplexer_2 (
    .in0(multiplexer_11_out), .in1({alu_1_result_2, alu_1_result}), .out(multiplexer_2_out), .sel(and_4_out));
  Register #(.width(32)) u_PC (.D(multiplexer_2_out), .en(multiplexer_1_out), .clk(clk), .Q(pc), .clr(Rest));
  Clock u_Clk (.out(clk));
  Adder #(.width(32)) adder_1 (.a(32'h4), .b(pc), .out(adder_1_out));  // open: cin, cout
  mem mem_1 (.MemAddress(pc), .clk(clk));  // open: MemWriteMask, MemWriteData, MemReadData
  oneClockDelay oneclockdelay_1 (
    .DataIn(adder_1_out), .clk(clk), .DataOut({oneclockdelay_1_dataout_2, oneclockdelay_1_dataout}));
  oneClockDelay oneclockdelay_2 (
    .DataIn(32'h11020), .clk(clk),
    .DataOut({oneclockdelay_2_dataout_5, oneclockdelay_2_dataout_4, oneclockdelay_2_dataout_3, oneclockdelay_2_dataout_2, oneclockdelay_2_dataout}));
  Multiplexer #(.width(5)) multiplexer_3 (
    .in0(oneclockdelay_2_dataout_4[20:16]), .in1(oneclockdelay_2_dataout_3), .out(multiplexer_3_out),
    .sel(id_ex_1_regdstout));
  assign bit_extender_1_out = {{6{1'b0}}, {oneclockdelay_2_dataout_4, oneclockdelay_2_dataout_3, oneclockdelay_2_dataout_2, oneclockdelay_2_dataout}};  // Bit_Extender bit_extender_1
  and and_1 (and_1_out, id_ex_1_jumpout, regfile_1_p5);
  Multiplexer #(.width(5)) multiplexer_4 (
    .in0(multiplexer_3_out), .in1({5{1'b1}}), .out(multiplexer_4_out), .sel(and_1_out));
  Multiplexer #(.width(32)) multiplexer_5 (
    .in0(multiplexer_15_out), .in1(pc), .out(multiplexer_5_out), .sel(and_1_out));
  Shifter #(.width(32)) shifter_1 (.in(bit_extender_1_out), .\dist (5'b00010), .out(shifter_1_out));
  assign bit_extender_2_out = {{28{1'b0}}, oneclockdelay_1_dataout_2};  // Bit_Extender bit_extender_2
  assign bit_extender_3_out = {{27{1'b0}}, oneclockdelay_2_dataout_2};  // Bit_Extender bit_extender_3
  Shifter #(.width(32)) shifter_2 (.in(bit_extender_2_out), .\dist (5'b11100), .out(shifter_2_out));
  assign xor_1_out = shifter_1_out ^ shifter_2_out;  // XOR_Gate xor_1, 32 bits wide
  Controller controller_1 (
    .Opcode(oneclockdelay_2_dataout_5), .RegDst(controller_1_regdst), .Branch(controller_1_branch),
    .Jump(controller_1_jump), .RegWrEn(controller_1_regwren), .AluSrc(controller_1_alusrc),
    .MemToReg(controller_1_memtoreg), .AluOpr(AO), .MemWrMask(controller_1_memwrmask), .LB(controller_1_lb));
  // regfile regfile_1: pin names not known; wires that end beside it: oneclockdelay_2_dataout_4[25:21], oneclockdelay_2_dataout_4[20:16], multiplexer_4_out, multiplexer_5_out, regfile_1_p5, clk, regfile_1_p7, regfile_1_p7, regfile_1_p9, regfile_1_p10
  signExtend signextend_1 (
    .Immd({oneclockdelay_2_dataout_3, oneclockdelay_2_dataout_2, oneclockdelay_2_dataout}),
    .Extended(signextend_1_extended));
  AluController alucontroller_1 (
    .func(oneclockdelay_2_dataout), .opcode(oneclockdelay_2_dataout_5), .aluOperation(AO),
    .ALU_out(alucontroller_1_alu_out), .sh_amount(alucontroller_1_sh_amount));
  ID_EX id_ex_1 (
    .clk(clk), .RegDstIn(controller_1_regdst), .BranchIn(controller_1_branch), .JumpIn(controller_1_jump),
    .RegWrEnIn(controller_1_regwren), .AluSrcIn(controller_1_alusrc), .MemToRegIn(controller_1_memtoreg),
    .AluOprIn(AO), .MemWrMaskIn(controller_1_memwrmask), .LBIn(controller_1_lb), .ReadData1In(regfile_1_p9),
    .ReadData2In(regfile_1_p10), .extendedBitsIn(bit_extender_3_out), .ExtendedIn(signextend_1_extended),
    .ALu_outIn(alucontroller_1_alu_out), .sh_amountIn(alucontroller_1_sh_amount),
    .RegDstOut(id_ex_1_regdstout), .BranchOut(id_ex_1_branchout), .JumpOut(id_ex_1_jumpout),
    .RegWrEnOut(regfile_1_p5), .AluSrcOut(id_ex_1_alusrcout), .MemToRegOut(memToReg), .AluOprOut(RType),
    .MemWrMaskOut(id_ex_1_memwrmaskout), .LBOut(LB), .ReadData1Out(id_ex_1_readdata1out),
    .ReadData2Out(id_ex_1_readdata2out), .extendedBitsOut(id_ex_1_extendedbitsout),
    .ExtendedOut(id_ex_1_extendedout), .Alu_outOut(id_ex_1_alu_outout), .sh_amountOut(id_ex_1_sh_amountout));
  and and_2 (and_2_out, ~id_ex_1_branchout, id_ex_1_alusrcout);  // AND_Gate
  Multiplexer #(.width(32)) multiplexer_6 (
    .in0(id_ex_1_readdata1out), .in1(id_ex_1_extendedbitsout), .out(multiplexer_6_out),
    .sel(id_ex_1_sh_amountout));
  Shifter #(.width(32)) shifter_3 (.in(id_ex_1_extendedout), .\dist (5'b00010), .out(shifter_3_out));
  Multiplexer #(.width(32)) multiplexer_7 (
    .in0(id_ex_1_readdata2out), .in1(id_ex_1_extendedout), .out(multiplexer_7_out), .sel(and_2_out));
  assign bit_extender_4_out = {{3{1'b0}}, alu_1_result};  // Bit_Extender bit_extender_4
  Adder #(.width(32)) adder_2 (
    .a({oneclockdelay_1_dataout_2, oneclockdelay_1_dataout}), .b(shifter_3_out), .out(adder_2_out));  // open: cin, cout
  Comparator #(.width(4)) comparator_1 (.a(id_ex_1_memwrmaskout), .b(4'b0001), .eq(comparator_1_eq));  // open: gt, lt
  Shifter #(.width(4)) shifter_4 (.in(id_ex_1_memwrmaskout), .\dist (alu_1_result), .out(shifter_4_out));
  Shifter #(.width(5)) shifter_5 (.in(bit_extender_4_out), .\dist (3'b011), .out(shifter_5_out));
  and and_3 (and_3_out, RType, alu_1_zero, comparator_2_eq);
  and and_4 (and_4_out, alu_1_zero, ~comparator_2_eq, RType);  // AND_Gate
  Shifter #(.width(32)) shifter_6 (.in(id_ex_1_readdata2out), .\dist (shifter_5_out), .out(shifter_6_out));
  Multiplexer #(.width(4)) multiplexer_8 (
    .in0(id_ex_1_memwrmaskout), .in1(shifter_4_out), .out(multiplexer_8_out), .sel(comparator_1_eq));
  ALU alu_1 (
    .ReadData1(multiplexer_6_out), .ReadData2(multiplexer_7_out), .ControlBits(id_ex_1_alu_outout),
    .Result({alu_1_result_2, alu_1_result}), .Zero(alu_1_zero));
  Multiplexer #(.width(32)) multiplexer_9 (
    .in0({oneclockdelay_1_dataout_2, oneclockdelay_1_dataout}), .in1(adder_2_out), .out(multiplexer_9_out),
    .sel(and_5_out));
  and and_5 (and_5_out, id_ex_1_branchout, alu_1_zero);
  Multiplexer #(.width(32)) multiplexer_10 (
    .in0(id_ex_1_readdata2out), .in1(shifter_6_out), .out(multiplexer_10_out), .sel(comparator_1_eq));
  Multiplexer #(.width(32)) multiplexer_11 (
    .in0(xor_1_out), .in1(multiplexer_9_out), .out(multiplexer_11_out), .sel(not_1_out));
  not not_1 (not_1_out, id_ex_1_jumpout);
  Comparator #(.width(32)) comparator_2 (
    .a({alu_1_result_2, alu_1_result}), .b({32{1'b1}}), .eq(comparator_2_eq));  // open: gt, lt
  Multiplexer #(.width(32)) multiplexer_12 (
    .in0(MemData), .in1({alu_1_result_2, alu_1_result}), .out(multiplexer_12_out));  // open: sel
  Comparator #(.width(4)) comparator_3 (.a(4'b1111), .b(multiplexer_8_out), .eq(comparator_3_eq));  // open: gt, lt
  or or_1 (or_1_out, cache_1_p5, comparator_3_eq);
  assign bit_extender_5_out = {{3{cache_1_p8}}, cache_1_p8};  // Bit_Extender bit_extender_5
  // Cache cache_1: pin names not known; wires that end beside it: clk, multiplexer_10_out, or_1_out, multiplexer_12_out, cache_1_p5, cache_1_p6, cache_1_p7, cache_1_p8, cache_1_p9
  memDelayed memdelayed_1 (
    .MemAddress(cache_1_p7), .MemWriteMask(bit_extender_5_out), .MemWriteData(cache_1_p9), .clk(clk),
    .MemReadData(MemData));
  assign bit_extender_6_out = {{24{1'b1}}, multiplexer_13_out};  // Bit_Extender bit_extender_6
  Multiplexer #(.select(2), .width(8)) multiplexer_13 (
    .in0(undriven[7:0]), .in1(undriven[15:8]), .in2(undriven[23:16]), .in3(undriven[31:24]),
    .out(multiplexer_13_out), .sel(alu_1_result));
  Multiplexer #(.width(32)) multiplexer_14 (
    .in0(undriven), .in1(bit_extender_6_out), .out(multiplexer_14_out), .sel(LB));
  Multiplexer #(.width(32)) multiplexer_15 (
    .in0({alu_1_result_2, alu_1_result}), .in1(cache_1_p6), .out(multiplexer_15_out), .sel(memToReg));
endmodule
